# Fritzing sketch Untitled Sketch 2 (saved by Fritzing 0.9.3b)

parts:
  U1 = NodeMCU V3.0
  LED1 = smd LED [color="Red (633nm)" package="0603 [SMD]"]

nets:
  N1: U1.D0, LED1.anode
  N2: U1.GND, LED1.cathode

custom parts:
  NodeMCU V3.0: ESP8266 based NodeMCU Modified for NodeMCUv3 Lolin (1.1 inch pcb spacing) added terminals to schematic svg
